# Fritzing sketch BeagleBone-Anemometer (saved by Fritzing 0.9.2b)
breadboards: 1

parts:
  BeagleBone1 = BeagleBone Black
  R1 = Resistor [tolerance=±0.1% resistance=1k package=THT]
  R2 = Resistor [tolerance=±0.1% resistance=1k package=THT]
  U1 = mystery part, 3 pins [chip_label=?]
  BAT1 = BC9VPC [package=bc9vpc]

nets:
  N1: BeagleBone1.no_name_yet#33, R1.Pin_1, R2.Pin_0
  N2: BeagleBone1.no_name_yet#34, R1.Pin_0, U1.pin1, BAT1.V-
  N3: R2.Pin_1, U1.pin2
  N4: U1.pin3, BAT1.V+

notes:
  Anemometer

custom parts:
  BeagleBone Black: BeagleBone Black rev. A5B
